// Logisim project basic_Full_8bitALU.circ as structural Verilog: 18 circuits, main circuit main
module main (
  input  [5:0] Ci,
  input  [7:0] InA,
  input  [7:0] InB,
  output [7:0] Res,
  output Co,
  output N,
  output Z,
  output E
);

  wire controlled_buffer_1_out, controlled_buffer_2_out, controlled_buffer_3_out, controlled_buffer_4_out,
       controlled_buffer_5_out, controlled_buffer_6_out, controlled_buffer_7_out, controlled_buffer_8_out,
       controlled_buffer_9_out, controlled_buffer_10_out, controlled_buffer_11_out, controlled_buffer_12_out,
       controlled_buffer_13_out, controlled_buffer_14_out, controlled_buffer_15_out,
       controlled_buffer_16_out, fulladder_1_co, fulladder_1_s, fulladder_2_co, fulladder_2_s,
       fulladder_3_co, fulladder_3_s, fulladder_4_co, fulladder_4_s, fulladder_5_co, fulladder_5_s,
       fulladder_6_co, fulladder_6_s, fulladder_7_co, fulladder_7_s, fulladder_8_s, fulladder_9_co,
       fulladder_10_co, fulladder_11_co, fulladder_12_co, fulladder_13_co, fulladder_14_co, fulladder_15_co,
       not_1_out, or_1_out, or_2_out, or_3_out, or_4_out, or_5_out, or_6_out, or_7_out, xor_1_out, xor_2_out,
       xor_3_out, xor_4_out, xor_5_out, xor_6_out, xor_7_out, xor_8_out, xor_9_out, xor_10_out, xor_11_out,
       xor_12_out, xor_13_out, xor_14_out, xor_15_out, xor_16_out;
  wire [3:0] fulladder_9_s, fulladder_13_s;
  wire [7:0] controlled_buffer_18_out, controlled_buffer_19_out, controlled_buffer_20_out,
       controlled_buffer_21_out, controlled_buffer_22_out, controlled_buffer_23_out, logicaland_1_s,
       logicalor_1_s, logicalxor_1_s;

  or or_1 (or_1_out, Ci[4], Ci[3]);
  OpErrorChecker operrorchecker_1 (.in_1(Ci), .out_2(E));
  or or_2 (or_2_out, Res[7], Res[6]);
  assign controlled_buffer_1_out = or_1_out ? InB[6] : 1'bz;  // Controlled_Buffer controlled_buffer_1
  assign controlled_buffer_2_out = or_1_out ? InB[7] : 1'bz;  // Controlled_Buffer controlled_buffer_2
  or or_3 (or_3_out, or_2_out, or_4_out);
  or or_4 (or_4_out, Res[5], Res[4]);
  assign controlled_buffer_3_out = or_1_out ? InB[2] : 1'bz;  // Controlled_Buffer controlled_buffer_3
  assign controlled_buffer_4_out = or_1_out ? InB[3] : 1'bz;  // Controlled_Buffer controlled_buffer_4
  assign controlled_buffer_5_out = or_1_out ? InB[4] : 1'bz;  // Controlled_Buffer controlled_buffer_5
  assign controlled_buffer_6_out = or_1_out ? InB[5] : 1'bz;  // Controlled_Buffer controlled_buffer_6
  nor nor_1 (Z, or_3_out, or_6_out);
  or or_5 (or_5_out, Res[3], Res[2]);
  assign controlled_buffer_7_out = or_1_out ? InB[0] : 1'bz;  // Controlled_Buffer controlled_buffer_7
  assign controlled_buffer_8_out = or_1_out ? InB[1] : 1'bz;  // Controlled_Buffer controlled_buffer_8
  or or_6 (or_6_out, or_5_out, or_7_out);
  or or_7 (or_7_out, Res[1], Res[0]);
  assign controlled_buffer_9_out = or_1_out ? InA[1] : 1'bz;  // Controlled_Buffer controlled_buffer_9
  assign controlled_buffer_10_out = or_1_out ? InA[0] : 1'bz;  // Controlled_Buffer controlled_buffer_10
  xor xor_1 (xor_1_out, controlled_buffer_7_out, Ci[3]);
  assign controlled_buffer_11_out = or_1_out ? InA[5] : 1'bz;  // Controlled_Buffer controlled_buffer_11
  assign controlled_buffer_12_out = or_1_out ? InA[4] : 1'bz;  // Controlled_Buffer controlled_buffer_12
  assign controlled_buffer_13_out = or_1_out ? InA[3] : 1'bz;  // Controlled_Buffer controlled_buffer_13
  assign controlled_buffer_14_out = or_1_out ? InA[2] : 1'bz;  // Controlled_Buffer controlled_buffer_14
  xor xor_2 (xor_2_out, controlled_buffer_8_out, Ci[3]);
  assign controlled_buffer_15_out = or_1_out ? InA[7] : 1'bz;  // Controlled_Buffer controlled_buffer_15
  assign controlled_buffer_16_out = or_1_out ? InA[6] : 1'bz;  // Controlled_Buffer controlled_buffer_16
  xor xor_3 (xor_3_out, controlled_buffer_3_out, Ci[3]);
  xor xor_4 (xor_4_out, controlled_buffer_4_out, Ci[3]);
  xor xor_5 (xor_5_out, controlled_buffer_5_out, Ci[3]);
  xor xor_6 (xor_6_out, controlled_buffer_6_out, Ci[3]);
  xor xor_7 (xor_7_out, controlled_buffer_1_out, Ci[3]);
  xor xor_8 (xor_8_out, controlled_buffer_2_out, Ci[3]);
  FullAdder fulladder_1 (
    .Ci(Ci[3]), .A(xor_1_out), .B(controlled_buffer_10_out), .S(fulladder_1_s), .Co(fulladder_1_co));
  FullAdder fulladder_2 (
    .Ci(fulladder_1_co), .A(xor_2_out), .B(controlled_buffer_9_out), .S(fulladder_2_s), .Co(fulladder_2_co));
  FullAdder fulladder_3 (
    .Ci(fulladder_2_co), .A(xor_3_out), .B(controlled_buffer_14_out), .S(fulladder_3_s), .Co(fulladder_3_co));
  FullAdder fulladder_4 (
    .Ci(fulladder_3_co), .A(xor_4_out), .B(controlled_buffer_13_out), .S(fulladder_4_s), .Co(fulladder_4_co));
  FullAdder fulladder_5 (
    .Ci(fulladder_4_co), .A(xor_5_out), .B(controlled_buffer_12_out), .S(fulladder_5_s), .Co(fulladder_5_co));
  FullAdder fulladder_6 (
    .Ci(fulladder_5_co), .A(xor_6_out), .B(controlled_buffer_11_out), .S(fulladder_6_s), .Co(fulladder_6_co));
  FullAdder fulladder_7 (
    .Ci(fulladder_6_co), .A(xor_7_out), .B(controlled_buffer_16_out), .S(fulladder_7_s), .Co(fulladder_7_co));
  FullAdder fulladder_8 (.Ci(fulladder_7_co), .A(xor_8_out), .B(controlled_buffer_15_out), .S(fulladder_8_s), .Co(Co));
  and and_1 (N, Ci[3], not_1_out);
  not not_1 (not_1_out, Co);
  xor xor_9 (xor_9_out, N, fulladder_1_s);
  xor xor_10 (xor_10_out, N, fulladder_2_s);
  xor xor_11 (xor_11_out, N, fulladder_3_s);
  xor xor_12 (xor_12_out, N, fulladder_4_s);
  xor xor_13 (xor_13_out, N, fulladder_5_s);
  xor xor_14 (xor_14_out, N, fulladder_6_s);
  xor xor_15 (xor_15_out, N, fulladder_7_s);
  xor xor_16 (xor_16_out, N, fulladder_8_s);
  FullAdder fulladder_9 (.Ci(N), .A(xor_9_out), .B(1'b0), .S(fulladder_9_s[0]), .Co(fulladder_9_co));
  FullAdder fulladder_10 (.Ci(fulladder_9_co), .A(xor_10_out), .B(1'b0), .S(fulladder_9_s[1]), .Co(fulladder_10_co));
  FullAdder fulladder_11 (.Ci(fulladder_10_co), .A(xor_11_out), .B(1'b0), .S(fulladder_9_s[2]), .Co(fulladder_11_co));
  FullAdder fulladder_12 (.Ci(fulladder_11_co), .A(xor_12_out), .B(1'b0), .S(fulladder_9_s[3]), .Co(fulladder_12_co));
  assign Res[3:0] = or_1_out ? fulladder_9_s : 4'bz;  // Controlled_Buffer controlled_buffer_17
  assign controlled_buffer_18_out = Ci[0] ? InA : 8'bz;  // Controlled_Buffer controlled_buffer_18
  assign controlled_buffer_19_out = Ci[0] ? InB : 8'bz;  // Controlled_Buffer controlled_buffer_19
  assign controlled_buffer_20_out = Ci[1] ? InA : 8'bz;  // Controlled_Buffer controlled_buffer_20
  assign controlled_buffer_21_out = Ci[1] ? InB : 8'bz;  // Controlled_Buffer controlled_buffer_21
  assign controlled_buffer_22_out = Ci[2] ? InA : 8'bz;  // Controlled_Buffer controlled_buffer_22
  assign controlled_buffer_23_out = Ci[2] ? InB : 8'bz;  // Controlled_Buffer controlled_buffer_23
  assign Res[7:4] = or_1_out ? fulladder_13_s : 4'bz;  // Controlled_Buffer controlled_buffer_24
  FullAdder fulladder_13 (.Ci(fulladder_12_co), .A(xor_13_out), .B(1'b0), .S(fulladder_13_s[0]), .Co(fulladder_13_co));
  FullAdder fulladder_14 (.Ci(fulladder_13_co), .A(xor_14_out), .B(1'b0), .S(fulladder_13_s[1]), .Co(fulladder_14_co));
  FullAdder fulladder_15 (.Ci(fulladder_14_co), .A(xor_15_out), .B(1'b0), .S(fulladder_13_s[2]), .Co(fulladder_15_co));
  FullAdder fulladder_16 (.Ci(fulladder_15_co), .A(xor_16_out), .B(1'b0), .S(fulladder_13_s[3]));  // open: Co
  logicalAND logicaland_1 (.A(controlled_buffer_18_out), .B(controlled_buffer_19_out), .S(logicaland_1_s));
  logicalOR logicalor_1 (.A(controlled_buffer_20_out), .B(controlled_buffer_21_out), .S(logicalor_1_s));
  logicalXOR logicalxor_1 (.A(controlled_buffer_22_out), .B(controlled_buffer_23_out), .S(logicalxor_1_s));
  assign Res = Ci[2] ? logicalxor_1_s : 8'bz;  // Controlled_Buffer controlled_buffer_25
  assign Res = Ci[1] ? logicalor_1_s : 8'bz;  // Controlled_Buffer controlled_buffer_26
  assign Res = Ci[0] ? logicaland_1_s : 8'bz;  // Controlled_Buffer controlled_buffer_27

  // Notes on the sheet:
  //   000001 = AND
  //   000010 =  OR
  //   000100 = XOR
  //   001000 = SUB
  //   010000 = ADD
  //   000000 = DNE
  //   Result
  //   Input A
  //   Carry Out
  //   Input B
  //   1 = negative
  //   1 = zero
  //   Op Error
endmodule

module logicalAND (
  input  [7:0] A,
  input  [7:0] B,
  output [7:0] S
);

  and and_1 (S[7], A[7], B[7]);
  and and_2 (S[6], A[6], B[6]);
  and and_3 (S[5], A[5], B[5]);
  and and_4 (S[4], A[4], B[4]);
  and and_5 (S[3], A[3], B[3]);
  and and_6 (S[2], A[2], B[2]);
  and and_7 (S[1], A[1], B[1]);
  and and_8 (S[0], A[0], B[0]);

  // Notes on the sheet:
  //   Logical AND
endmodule

module logicalOR (
  input  [7:0] A,
  input  [7:0] B,
  output [7:0] S
);

  or or_1 (S[7], A[7], B[7]);
  or or_2 (S[6], A[6], B[6]);
  or or_3 (S[5], A[5], B[5]);
  or or_4 (S[4], A[4], B[4]);
  or or_5 (S[3], A[3], B[3]);
  or or_6 (S[2], A[2], B[2]);
  or or_7 (S[1], A[1], B[1]);
  or or_8 (S[0], A[0], B[0]);

  // Notes on the sheet:
  //   Logical OR
endmodule

module logicalXOR (
  input  [7:0] A,
  input  [7:0] B,
  output [7:0] S
);

  xor xor_1 (S[7], A[7], B[7]);
  xor xor_2 (S[6], A[6], B[6]);
  xor xor_3 (S[5], A[5], B[5]);
  xor xor_4 (S[4], A[4], B[4]);
  xor xor_5 (S[3], A[3], B[3]);
  xor xor_6 (S[2], A[2], B[2]);
  xor xor_7 (S[1], A[1], B[1]);
  xor xor_8 (S[0], A[0], B[0]);

  // Notes on the sheet:
  //   Logical XOR
endmodule

module logicalNAND (
  input  [7:0] A,
  input  [7:0] B,
  output [7:0] S
);

  nand nand_1 (S[7], A[7], B[7]);
  nand nand_2 (S[6], A[6], B[6]);
  nand nand_3 (S[5], A[5], B[5]);
  nand nand_4 (S[4], A[4], B[4]);
  nand nand_5 (S[3], A[3], B[3]);
  nand nand_6 (S[2], A[2], B[2]);
  nand nand_7 (S[1], A[1], B[1]);
  nand nand_8 (S[0], A[0], B[0]);

  // Notes on the sheet:
  //   Logical NAND
endmodule

module logicalNOR (
  input  [7:0] A,
  input  [7:0] B,
  output [7:0] S
);

  nor nor_1 (S[7], A[7], B[7]);
  nor nor_2 (S[6], A[6], B[6]);
  nor nor_3 (S[5], A[5], B[5]);
  nor nor_4 (S[4], A[4], B[4]);
  nor nor_5 (S[3], A[3], B[3]);
  nor nor_6 (S[2], A[2], B[2]);
  nor nor_7 (S[1], A[1], B[1]);
  nor nor_8 (S[0], A[0], B[0]);

  // Notes on the sheet:
  //   Logical NOR
endmodule

module FullAdder (
  input  Ci,
  input  A,
  input  B,
  output S,
  output Co
);

  wire and_1_out, and_2_out, xor_1_out;

  and and_1 (and_1_out, B, A);
  xor xor_1 (xor_1_out, A, B);
  and and_2 (and_2_out, Ci, xor_1_out);
  xor xor_2 (S, xor_1_out, Ci);
  or or_1 (Co, and_2_out, and_1_out);

  // Notes on the sheet:
  //   Full Adder
endmodule

module EdgeDetector (
  output O
);

  wire clock_1_out, not_1_out, not_2_out, not_3_out;

  Clock clock_1 (.out(clock_1_out));
  not not_1 (not_1_out, clock_1_out);
  not not_2 (not_2_out, not_1_out);
  not not_3 (not_3_out, not_2_out);
  and and_1 (O, clock_1_out, not_3_out);

  // Notes on the sheet:
  //   Rising Edge Detector
endmodule

module FullLogicalUnit (
  input  [3:0] CTRL,
  input  B,
  input  A,
  input  Ci,
  output Co,
  output R
);

  wire and_1_out, and_2_out, and_3_out, and_4_out, and_5_out, and_6_out, or_3_out, or_4_out, xor_1_out,
       xor_2_out;

  and and_1 (and_1_out, A, B);
  or or_1 (Co, and_1_out, and_2_out);
  and and_2 (and_2_out, xor_1_out, Ci);
  or or_2 (R, and_3_out, or_4_out);
  xor xor_1 (xor_1_out, B, A);
  xor xor_2 (xor_2_out, Ci, xor_1_out);
  and and_3 (and_3_out, xor_2_out, CTRL[2]);
  or or_3 (or_3_out, B, A);
  and and_4 (and_4_out, or_3_out, CTRL[1]);
  or or_4 (or_4_out, and_4_out, and_6_out);
  and and_5 (and_5_out, B, A);
  and and_6 (and_6_out, and_5_out, CTRL[0]);

  // Notes on the sheet:
  //   Full Adder + Bitwise Logic
endmodule

module FourBitAdder (
  input  Ci,
  input  [3:0] A,
  input  [3:0] B,
  output [3:0] S,
  output Co
);

  wire fulladder_1_co, fulladder_2_co, fulladder_3_co;

  FullAdder fulladder_1 (.Ci(Ci), .A(A[0]), .B(B[0]), .S(S[0]), .Co(fulladder_1_co));
  FullAdder fulladder_2 (.Ci(fulladder_3_co), .A(A[2]), .B(B[2]), .S(S[2]), .Co(fulladder_2_co));
  FullAdder fulladder_3 (.Ci(fulladder_1_co), .A(A[1]), .B(B[1]), .S(S[1]), .Co(fulladder_3_co));
  FullAdder fulladder_4 (.Ci(fulladder_2_co), .A(A[3]), .B(B[3]), .S(S[3]), .Co(Co));
endmodule

module DCE_ByteAdderSubtractor (
  input  Sub,
  input  [7:0] A,
  input  [7:0] B,
  output TwosComp,
  output Sign,
  output [7:0] Sum,
  output Overflow,
  output Zero
);

  wire fulladder_1_co, fulladder_2_co, fulladder_3_co, fulladder_4_co, fulladder_6_co, fulladder_7_co,
       fulladder_8_co, not_1_out, or_1_out, or_2_out, or_3_out, or_4_out, or_5_out, or_6_out, xor_1_out,
       xor_2_out, xor_3_out, xor_4_out, xor_5_out, xor_6_out, xor_7_out, xor_8_out;

  or or_1 (or_1_out, or_2_out, or_3_out);
  or or_2 (or_2_out, Sum[3], Sum[2]);
  xor xor_1 (xor_1_out, B[3], Sub);
  nor nor_1 (Zero, or_1_out, or_4_out);
  or or_3 (or_3_out, Sum[1], Sum[0]);
  and and_1 (Sign, not_1_out, Sub);
  or or_4 (or_4_out, or_5_out, or_6_out);
  or or_5 (or_5_out, Sum[4], Sum[5]);
  not not_1 (not_1_out, fulladder_1_co);
  or or_6 (or_6_out, Sum[6], Sum[7]);
  FullAdder fulladder_1 (.Ci(fulladder_2_co), .A(A[3]), .B(xor_1_out), .S(Sum[3]), .Co(fulladder_1_co));
  xor xor_2 (xor_2_out, B[2], Sub);
  FullAdder fulladder_2 (.Ci(fulladder_3_co), .A(A[2]), .B(xor_2_out), .S(Sum[2]), .Co(fulladder_2_co));
  xor xor_3 (xor_3_out, B[1], Sub);
  FullAdder fulladder_3 (.Ci(fulladder_4_co), .A(A[1]), .B(xor_3_out), .S(Sum[1]), .Co(fulladder_3_co));
  xor xor_4 (xor_4_out, B[0], Sub);
  FullAdder fulladder_4 (.Ci(Sub), .A(A[0]), .B(xor_4_out), .S(Sum[0]), .Co(fulladder_4_co));
  xor xor_5 (xor_5_out, B[7], Sub);
  FullAdder fulladder_5 (.Ci(fulladder_6_co), .A(A[7]), .B(xor_5_out), .S(Sum[7]), .Co(Overflow));
  xor xor_6 (xor_6_out, B[6], Sub);
  FullAdder fulladder_6 (.Ci(fulladder_7_co), .A(A[6]), .B(xor_6_out), .S(Sum[6]), .Co(fulladder_6_co));
  xor xor_7 (xor_7_out, B[5], Sub);
  FullAdder fulladder_7 (.Ci(fulladder_8_co), .A(A[5]), .B(xor_7_out), .S(Sum[5]), .Co(fulladder_7_co));
  xor xor_8 (xor_8_out, B[4], Sub);
  FullAdder fulladder_8 (.Ci(fulladder_1_co), .A(A[4]), .B(xor_8_out), .S(Sum[4]), .Co(fulladder_8_co));

  assign TwosComp = Sign;

  // Notes on the sheet:
  //   8-Bit Arithemetic Logic Unit (ALU) V2.0
endmodule

module OpErrorChecker (
  input  [5:0] in_1,
  output out_2
);

  wire not_1_out, or_1_out, or_2_out, or_3_out, or_4_out, or_5_out, xor_1_out, xor_2_out, xor_3_out,
       xor_4_out, xor_5_out;

  or or_1 (or_1_out, in_1[5], in_1[4]);
  or or_2 (or_2_out, or_1_out, or_3_out);
  or or_3 (or_3_out, or_4_out, or_5_out);
  or or_4 (or_4_out, in_1[3], in_1[2]);
  or or_5 (or_5_out, in_1[1], in_1[0]);
  xor xor_1 (xor_1_out, xor_2_out, xor_4_out);
  xor xor_2 (xor_2_out, in_1[5], in_1[4]);
  assign out_2 = or_2_out ? not_1_out : 1'bz;  // Controlled_Buffer controlled_buffer_1
  not not_1 (not_1_out, xor_3_out);
  xor xor_3 (xor_3_out, xor_1_out, xor_5_out);
  xor xor_4 (xor_4_out, in_1[3], in_1[2]);
  xor xor_5 (xor_5_out, in_1[1], in_1[0]);
endmodule

module Encoder4by2 (
  input  I0,
  input  I1,
  input  I2,
  input  I3,
  output O0,
  output O1
);

  or or_1 (O0, I3, I1);
  or or_2 (O1, I2, I3);
endmodule

module Encoder8by3 (
  input  I0,
  input  I1,
  input  I2,
  input  I3,
  input  I4,
  input  I5,
  input  I6,
  input  I7,
  output O0,
  output O1,
  output O2
);

  wire or_1_out, or_2_out, or_3_out, or_4_out, or_5_out, or_6_out;

  or or_1 (or_1_out, I1, I3);
  or or_2 (or_2_out, I5, I7);
  or or_3 (or_3_out, I2, I3);
  or or_4 (or_4_out, I6, I7);
  or or_5 (or_5_out, I4, I5);
  or or_6 (or_6_out, I6, I7);
  or or_7 (O0, or_1_out, or_2_out);
  or or_8 (O1, or_3_out, or_4_out);
  or or_9 (O2, or_5_out, or_6_out);
endmodule

module Decoder2by4 (
  input  I0,
  input  I1,
  input  E,
  output O0,
  output O1,
  output O2,
  output O3
);

  wire not_1_out, not_2_out;

  not not_1 (not_1_out, I0);
  not not_2 (not_2_out, I1);
  and and_1 (O0, not_1_out, E, not_2_out);
  and and_2 (O1, not_2_out, E, I0);
  and and_3 (O2, not_1_out, E, I1);
  and and_4 (O3, I1, E, I0);
endmodule

module Decoder3by8 (
  input  I0,
  input  I1,
  input  I2,
  output O7,
  output O6,
  output O5,
  output O4,
  output O3,
  output O2,
  output O1,
  output O0
);

  wire not_1_out;

  not not_1 (not_1_out, I2);
  Decoder2by4 decoder2by4_1 (.I0(I0), .I1(I1), .E(I2), .O0(O4), .O1(O5), .O2(O6), .O3(O7));
  Decoder2by4 decoder2by4_2 (.I0(I0), .I1(I1), .E(not_1_out), .O0(O0), .O1(O1), .O2(O2), .O3(O3));
endmodule

module MUX4by1 (
  input  S0,
  input  S1,
  input  I0,
  input  I1,
  input  I2,
  input  I3,
  output O
);

  wire and_1_out, and_2_out, and_3_out, and_4_out, decoder2by4_1_o0, decoder2by4_1_o1, decoder2by4_1_o2,
       decoder2by4_1_o3, or_1_out, or_2_out;

  Decoder2by4 decoder2by4_1 (
    .I0(S0), .I1(S1), .E(1'b1), .O0(decoder2by4_1_o0), .O1(decoder2by4_1_o1), .O2(decoder2by4_1_o2),
    .O3(decoder2by4_1_o3));
  and and_1 (and_1_out, I0, decoder2by4_1_o0);
  and and_2 (and_2_out, I1, decoder2by4_1_o1);
  and and_3 (and_3_out, I2, decoder2by4_1_o2);
  and and_4 (and_4_out, I3, decoder2by4_1_o3);
  or or_1 (or_1_out, and_1_out, and_2_out);
  or or_2 (or_2_out, and_3_out, and_4_out);
  or or_3 (O, or_1_out, or_2_out);
endmodule

module MUX8by1 (
  input  S0,
  input  S1,
  input  S2,
  input  I0,
  input  I1,
  input  I2,
  input  I3,
  input  I4,
  input  I5,
  input  I6,
  input  I7,
  output O
);

  wire and_1_out, and_2_out, and_3_out, and_4_out, and_5_out, and_6_out, and_7_out, and_8_out,
       decoder3by8_1_o0, decoder3by8_1_o1, decoder3by8_1_o2, decoder3by8_1_o3, decoder3by8_1_o4,
       decoder3by8_1_o5, decoder3by8_1_o6, decoder3by8_1_o7, or_1_out, or_2_out, or_3_out, or_4_out,
       or_5_out, or_6_out;

  Decoder3by8 decoder3by8_1 (
    .I0(S0), .I1(S1), .I2(S2), .O7(decoder3by8_1_o7), .O6(decoder3by8_1_o6), .O5(decoder3by8_1_o5),
    .O4(decoder3by8_1_o4), .O3(decoder3by8_1_o3), .O2(decoder3by8_1_o2), .O1(decoder3by8_1_o1),
    .O0(decoder3by8_1_o0));
  and and_1 (and_1_out, I0, decoder3by8_1_o0);
  and and_2 (and_2_out, I1, decoder3by8_1_o1);
  and and_3 (and_3_out, I2, decoder3by8_1_o2);
  and and_4 (and_4_out, I3, decoder3by8_1_o3);
  and and_5 (and_5_out, I4, decoder3by8_1_o4);
  and and_6 (and_6_out, I5, decoder3by8_1_o5);
  and and_7 (and_7_out, I6, decoder3by8_1_o6);
  and and_8 (and_8_out, I7, decoder3by8_1_o7);
  or or_1 (or_1_out, and_1_out, and_2_out);
  or or_2 (or_2_out, and_3_out, and_4_out);
  or or_3 (or_3_out, and_5_out, and_6_out);
  or or_4 (or_4_out, and_7_out, and_8_out);
  or or_5 (or_5_out, or_1_out, or_2_out);
  or or_6 (or_6_out, or_3_out, or_4_out);
  or or_7 (O, or_5_out, or_6_out);
endmodule
